// Digital circuit ALU.dig as structural Verilog
module ALU (
  input  [15:0] Left,
  input  [15:0] Right,
  output [15:0] result,
  output greater,
  output eq,
  output less
);

  Add #(.Bits(16)) add_1 (.a(Left), .b(Right), .c_i(1'b0), .s(result));  // open: c_o
  Comparator #(.Bits(16)) comparator_1 (.a(Left), .b(Right), .gt(greater), .eq(eq), .lt(less));
endmodule
