// Digital circuit CPU.dig as structural Verilog
module CPU (
  input  [3:0] in_13,
  input  [3:0] in_14,
  input  [3:0] in_15,
  input  [3:0] in_16,
  input  [3:0] in_17,
  input  [3:0] in_18,
  input  [3:0] in_19,
  input  [3:0] in_20,
  input  [3:0] in_21,
  input  [3:0] in_22,
  input  [3:0] in_23,
  input  [3:0] in_24,
  input  [3:0] in_25,
  input  [3:0] in_26,
  output [15:0] out_1,
  output [3:0] out_2,
  output [1:0] out_3,
  output [1:0] out_4,
  output [1:0] out_5,
  output [7:0] out_6,
  output [3:0] out_7,
  output [15:0] out_8,
  output [15:0] out_9,
  output [15:0] out_10,
  output [15:0] out_11,
  output [15:0] out_12
);

  wire alu_1_eq, alu_1_greater, alu_1_less, and_1_out, branch_unit_1_branch, button_1_out,
       control_unit_1_alusrc, control_unit_1_branch, control_unit_1_jump, control_unit_1_memread,
       control_unit_1_memtoreg, control_unit_1_memwrite, control_unit_1_regdst, control_unit_1_regwrite,
       display_driver_inst_1_1_p1, display_driver_inst_1_1_p2, display_driver_inst_1_1_p3,
       display_driver_inst_1_1_p4, display_driver_inst_1_1_p5, display_driver_reg_1_p1,
       display_driver_reg_1_p2, display_driver_reg_2_p1, display_driver_reg_2_p2, display_driver_reg_3_p1,
       display_driver_reg_3_p2, display_driver_reg_4_p1, display_driver_reg_4_p2, display_driver_reg_5_p1,
       display_driver_reg_5_p2, display_driver_reg_6_p1, display_driver_reg_6_p2, display_driver_reg_7_p1,
       display_driver_reg_7_p2, display_driver_reg_8_p1, display_driver_reg_8_p2, display_driver_reg_9_p1,
       display_driver_reg_9_p2, display_driver_reg_10_p1, display_driver_reg_10_p2, display_driver_reg_11_p1,
       display_driver_reg_11_p2, display_driver_reg_12_p1, display_driver_reg_12_p2,
       display_driver_reg_13_p1, display_driver_reg_13_p2, or_1_out;
  wire [1:0] aluop, multiplexer_2_out, multiplexer_3_out;
  wire [3:0] add_1_s, decoder_1_p6, display_driver_reg_1_d1, display_driver_reg_1_d2,
       display_driver_reg_2_d1, display_driver_reg_2_d2, display_driver_reg_3_d1, display_driver_reg_3_d2,
       display_driver_reg_4_d1, display_driver_reg_4_d2, display_driver_reg_5_d1, display_driver_reg_5_d2,
       display_driver_reg_6_d1, display_driver_reg_6_d2, display_driver_reg_7_d1, display_driver_reg_7_d2,
       display_driver_reg_8_d1, display_driver_reg_8_d2, display_driver_reg_9_d1, display_driver_reg_9_d2,
       display_driver_reg_10_d1, display_driver_reg_10_d2, display_driver_reg_11_d1,
       display_driver_reg_11_d2, display_driver_reg_12_d1, display_driver_reg_12_d2,
       display_driver_reg_13_d1, display_driver_reg_13_d2, multiplexer_1_out;
  wire [11:4] decoder_1_p6_2;
  wire [15:0] alu_1_result, bitextender_1_out, display_driver_inst_1_1_d1, display_driver_inst_1_1_d2,
       display_driver_inst_1_1_d3, display_driver_inst_1_1_d4, display_driver_inst_1_1_d5, multiplexer_4_out,
       multiplexer_5_out, ramdualport_1_d, register_file_1_reg_1_value, register_file_1_reg_2_value;

  Add #(.Bits(4)) add_1 (.a(out_6[3:0]), .b(out_7), .c_i(1'b0), .s(add_1_s));  // open: c_o
  Multiplexer #(.Bits(4)) multiplexer_1 (.sel(and_1_out), .in_0(decoder_1_p6), .in_1(add_1_s), .out(multiplexer_1_out));
  and and_1 (and_1_out, control_unit_1_branch, branch_unit_1_branch);
  Button button_1 (.out(button_1_out));
  or or_1 (or_1_out, control_unit_1_jump, branch_unit_1_branch);
  Program_Counter program_counter_1 (
    .address_i(multiplexer_1_out), .write(or_1_out), .CLK(button_1_out), .address_o(out_7));
  Program_Memory program_memory_1 (.address(out_7), .instruction(out_8));
  // Decoder decoder_1: pin names not known; wires that end beside it: out_8, out_2, out_3, out_4, {out_5, out_6[5:0]}, {decoder_1_p6_2, decoder_1_p6}
  SixteenSeg sixteenseg_1 (.led(display_driver_inst_1_1_d1), .dp(display_driver_inst_1_1_p1));
  SixteenSeg sixteenseg_2 (.led(display_driver_inst_1_1_d2), .dp(display_driver_inst_1_1_p2));
  display_driver_inst_1 display_driver_inst_1_1 (
    .D1(display_driver_inst_1_1_d1), .P1(display_driver_inst_1_1_p1), .D2(display_driver_inst_1_1_d2),
    .P2(display_driver_inst_1_1_p2), .D3(display_driver_inst_1_1_d3), .P3(display_driver_inst_1_1_p3),
    .D4(display_driver_inst_1_1_d4), .P4(display_driver_inst_1_1_p4), .D5(display_driver_inst_1_1_d5),
    .P5(display_driver_inst_1_1_p5), .Opcode(in_13));
  Control_Unit control_unit_1 (
    .opcode(out_2), .RegDst(control_unit_1_regdst), .Jump(control_unit_1_jump),
    .Branch(control_unit_1_branch), .MemRead(control_unit_1_memread), .MemtoReg(control_unit_1_memtoreg),
    .MemWrite(control_unit_1_memwrite), .ALUSrc(control_unit_1_alusrc), .RegWrite(control_unit_1_regwrite),
    .ALUOp(aluop));
  SixteenSeg sixteenseg_3 (.led(display_driver_inst_1_1_d3), .dp(display_driver_inst_1_1_p3));
  SixteenSeg sixteenseg_4 (.led(display_driver_inst_1_1_d4), .dp(display_driver_inst_1_1_p4));
  Multiplexer #(.Bits(2)) multiplexer_2 (
    .sel(control_unit_1_regdst), .in_0(out_4), .in_1(out_5), .out(multiplexer_2_out));
  BitExtender bitextender_1 (.in({out_5, out_6[5:0]}), .out(bitextender_1_out));
  SixteenSeg sixteenseg_5 (.led(display_driver_inst_1_1_d5), .dp(display_driver_inst_1_1_p5));
  Seven_Seg_Hex seven_seg_hex_1 (.d(display_driver_reg_1_d1), .dp(display_driver_reg_1_p1));
  Seven_Seg_Hex seven_seg_hex_2 (.d(display_driver_reg_1_d2), .dp(display_driver_reg_1_p2));
  display_driver_reg display_driver_reg_1 (
    .Opcode(in_14), .D1(display_driver_reg_1_d1), .P1(display_driver_reg_1_p1), .D2(display_driver_reg_1_d2),
    .P2(display_driver_reg_1_p2));
  Multiplexer #(.Bits(2)) multiplexer_3 (
    .sel(control_unit_1_memtoreg), .in_0(multiplexer_2_out), .in_1(out_3), .out(multiplexer_3_out));
  Seven_Seg_Hex seven_seg_hex_3 (.d(display_driver_reg_2_d1), .dp(display_driver_reg_2_p1));
  Register_File register_file_1 (
    .Reg_1_Read(out_3), .Reg_2_Read(out_4), .Reg_Write(multiplexer_3_out), .data(out_1), .CLK(button_1_out),
    .Write_Enable(control_unit_1_regwrite), .Reg_1_Value(register_file_1_reg_1_value),
    .Reg_2_Value(register_file_1_reg_2_value), .R1(out_9), .R2(out_10), .R3(out_11), .R4(out_12));
  Seven_Seg_Hex seven_seg_hex_4 (.d(display_driver_reg_2_d2), .dp(display_driver_reg_2_p2));
  display_driver_reg display_driver_reg_2 (
    .Opcode(in_15), .D1(display_driver_reg_2_d1), .P1(display_driver_reg_2_p1), .D2(display_driver_reg_2_d2),
    .P2(display_driver_reg_2_p2));
  Seven_Seg_Hex seven_seg_hex_5 (.d(display_driver_reg_3_d1), .dp(display_driver_reg_3_p1));
  Seven_Seg_Hex seven_seg_hex_6 (.d(display_driver_reg_3_d2), .dp(display_driver_reg_3_p2));
  display_driver_reg display_driver_reg_3 (
    .Opcode(in_16), .D1(display_driver_reg_3_d1), .P1(display_driver_reg_3_p1), .D2(display_driver_reg_3_d2),
    .P2(display_driver_reg_3_p2));
  Seven_Seg_Hex seven_seg_hex_7 (.d(display_driver_reg_4_d1), .dp(display_driver_reg_4_p1));
  Seven_Seg_Hex seven_seg_hex_8 (.d(display_driver_reg_4_d2), .dp(display_driver_reg_4_p2));
  Seven_Seg_Hex seven_seg_hex_9 (.d(display_driver_reg_5_d1), .dp(display_driver_reg_5_p1));
  display_driver_reg display_driver_reg_4 (
    .Opcode(in_17), .D1(display_driver_reg_4_d1), .P1(display_driver_reg_4_p1), .D2(display_driver_reg_4_d2),
    .P2(display_driver_reg_4_p2));
  Seven_Seg_Hex seven_seg_hex_10 (.d(display_driver_reg_5_d2), .dp(display_driver_reg_5_p2));
  Seven_Seg_Hex seven_seg_hex_11 (.d(display_driver_reg_6_d1), .dp(display_driver_reg_6_p1));
  display_driver_reg display_driver_reg_5 (
    .Opcode(in_18), .D1(display_driver_reg_5_d1), .P1(display_driver_reg_5_p1), .D2(display_driver_reg_5_d2),
    .P2(display_driver_reg_5_p2));
  Multiplexer #(.Bits(16)) multiplexer_4 (
    .sel(control_unit_1_alusrc), .in_0(register_file_1_reg_2_value), .in_1(bitextender_1_out),
    .out(multiplexer_4_out));
  Seven_Seg_Hex seven_seg_hex_12 (.d(display_driver_reg_6_d2), .dp(display_driver_reg_6_p2));
  Seven_Seg_Hex seven_seg_hex_13 (.d(display_driver_reg_7_d1), .dp(display_driver_reg_7_p1));
  display_driver_reg display_driver_reg_6 (
    .Opcode(in_19), .D1(display_driver_reg_6_d1), .P1(display_driver_reg_6_p1), .D2(display_driver_reg_6_d2),
    .P2(display_driver_reg_6_p2));
  Seven_Seg_Hex seven_seg_hex_14 (.d(display_driver_reg_7_d2), .dp(display_driver_reg_7_p2));
  display_driver_reg display_driver_reg_7 (
    .Opcode(in_20), .D1(display_driver_reg_7_d1), .P1(display_driver_reg_7_p1), .D2(display_driver_reg_7_d2),
    .P2(display_driver_reg_7_p2));
  Multiplexer #(.Bits(16)) multiplexer_5 (
    .sel(control_unit_1_memtoreg), .in_0(register_file_1_reg_1_value), .in_1({16{1'b0}}),
    .out(multiplexer_5_out));
  Seven_Seg_Hex seven_seg_hex_15 (.d(display_driver_reg_8_d1), .dp(display_driver_reg_8_p1));
  Seven_Seg_Hex seven_seg_hex_16 (.d(display_driver_reg_8_d2), .dp(display_driver_reg_8_p2));
  display_driver_reg display_driver_reg_8 (
    .Opcode(in_21), .D1(display_driver_reg_8_d1), .P1(display_driver_reg_8_p1), .D2(display_driver_reg_8_d2),
    .P2(display_driver_reg_8_p2));
  ALU alu_1 (
    .Left(multiplexer_5_out), .Right(multiplexer_4_out), .ALUOp(aluop), .result(alu_1_result),
    .greater(alu_1_greater), .eq(alu_1_eq), .less(alu_1_less));
  Seven_Seg_Hex seven_seg_hex_17 (.d(display_driver_reg_9_d1), .dp(display_driver_reg_9_p1));
  Seven_Seg_Hex seven_seg_hex_18 (.d(display_driver_reg_9_d2), .dp(display_driver_reg_9_p2));
  display_driver_reg display_driver_reg_9 (
    .Opcode(in_22), .D1(display_driver_reg_9_d1), .P1(display_driver_reg_9_p1), .D2(display_driver_reg_9_d2),
    .P2(display_driver_reg_9_p2));
  Seven_Seg_Hex seven_seg_hex_19 (.d(display_driver_reg_10_d1), .dp(display_driver_reg_10_p1));
  Seven_Seg_Hex seven_seg_hex_20 (.d(display_driver_reg_10_d2), .dp(display_driver_reg_10_p2));
  display_driver_reg display_driver_reg_10 (
    .Opcode(in_23), .D1(display_driver_reg_10_d1), .P1(display_driver_reg_10_p1),
    .D2(display_driver_reg_10_d2), .P2(display_driver_reg_10_p2));
  Seven_Seg_Hex seven_seg_hex_21 (.d(display_driver_reg_11_d1), .dp(display_driver_reg_11_p1));
  Seven_Seg_Hex seven_seg_hex_22 (.d(display_driver_reg_11_d2), .dp(display_driver_reg_11_p2));
  display_driver_reg display_driver_reg_11 (
    .Opcode(in_24), .D1(display_driver_reg_11_d1), .P1(display_driver_reg_11_p1),
    .D2(display_driver_reg_11_d2), .P2(display_driver_reg_11_p2));
  Branch_Unit branch_unit_1 (
    .greater(alu_1_greater), .eq(alu_1_eq), .less(alu_1_less), .Opcode(out_2), .Branch(branch_unit_1_branch));
  Seven_Seg_Hex seven_seg_hex_23 (.d(display_driver_reg_12_d1), .dp(display_driver_reg_12_p1));
  Seven_Seg_Hex seven_seg_hex_24 (.d(display_driver_reg_12_d2), .dp(display_driver_reg_12_p2));
  display_driver_reg display_driver_reg_12 (
    .Opcode(in_25), .D1(display_driver_reg_12_d1), .P1(display_driver_reg_12_p1),
    .D2(display_driver_reg_12_d2), .P2(display_driver_reg_12_p2));
  Seven_Seg_Hex seven_seg_hex_25 (.d(display_driver_reg_13_d1), .dp(display_driver_reg_13_p1));
  Seven_Seg_Hex seven_seg_hex_26 (.d(display_driver_reg_13_d2), .dp(display_driver_reg_13_p2));
  display_driver_reg display_driver_reg_13 (
    .Opcode(in_26), .D1(display_driver_reg_13_d1), .P1(display_driver_reg_13_p1),
    .D2(display_driver_reg_13_d2), .P2(display_driver_reg_13_p2));
  RAMDualPort #(.AddrBits(16), .Bits(16)) ramdualport_1 (
    .A(alu_1_result), .Din(register_file_1_reg_2_value), .str(control_unit_1_memwrite), .C(button_1_out),
    .ld(control_unit_1_memread), .D(ramdualport_1_d));
  Multiplexer #(.Bits(16)) multiplexer_6 (
    .sel(control_unit_1_memread), .in_0(alu_1_result), .in_1(ramdualport_1_d), .out(out_1));

  assign out_6[7:6] = out_5;

  // Other names for the same wires on the sheet: imm[7:0] = {out_5, out_6[5:0]}; rd[1:0] = out_5;
  //   instruction[15:0] = out_8; opcode[3:0] = out_2; pc[3:0] = out_7; R1[15:0] = out_9; R2[15:0] = out_10;
  //   R3[15:0] = out_11; R4[15:0] = out_12; rs[1:0] = out_3; rt[1:0] = out_4
endmodule
