// Digital circuit Control-Unit.dig as structural Verilog
module Control_Unit (
  input  [3:0] opcode,
  output RegDst,
  output Jump,
  output Branch,
  output MemRead,
  output MemtoReg,
  output MemWrite,
  output ALUSrc,
  output RegWrite,
  output [1:0] ALUOp
);

  ROM #(.AddrBits(4), .Bits(8)) rom_1 (
    .A(opcode), .sel(1'b1), .D({RegWrite, ALUSrc, MemtoReg, MemWrite, MemRead, Branch, Jump, RegDst}));

  assign ALUOp = 2'b00;

  // Notes on the sheet:
  //   As a temporary solution decode the opcode 
  //   with a ROM. Later use logic gates.
  //   contents of rom_1 (hex, n*v repeats v):
  //   81,c0,e8,50,42
endmodule
