// Digital circuit Decoder.dig as structural Verilog
module Decoder (
  input  [15:0] instruction,
  output [3:0] opcode,
  output [1:0] rs,
  output [1:0] rt,
  output [7:0] immediate
);


  assign immediate = instruction[15:8];
  assign opcode = instruction[3:0];
  assign rs = instruction[5:4];
  assign rt = instruction[7:6];
endmodule
