// Digital circuit Program Counter.dig as structural Verilog
module Program_Counter (
  input  [3:0] address_i,
  input  write,
  input  CLK,
  output [3:0] address_o
);

  CounterPreset #(.Bits(4)) counterpreset_1 (
    .en(1'b1), .C(CLK), .dir(1'b0), .in(address_i), .ld(write), .clr(1'b0), .out(address_o));  // open: ovf
endmodule
