// Digital circuit Program Memory.dig as structural Verilog
module Program_Memory (
  input  [15:0] address,
  output [15:0] instruction
);

  EEPROMDualPort #(.AddrBits(16), .isProgramMemory("true"), .Bits(16)) \program  (
    .A(address), .Din({16{1'b0}}), .str(1'b0), .C(1'b0), .ld(1'b1), .D(instruction));

  // Notes on the sheet:
  //   contents of program (hex, n*v repeats v):
  //   9008,9404,9802,9c01,7*0,4001
endmodule
