// Digital circuit Register File.dig as structural Verilog
module Register_File (
  input  [1:0] Reg_1_Read,
  input  [1:0] Reg_2_Read,
  input  [1:0] Reg_Write,
  input  [15:0] data,
  input  CLK,
  output [15:0] Reg_1_Value,
  output [15:0] Reg_2_Value
);

  wire decoder_1_out_0, decoder_1_out_1, decoder_1_out_2, decoder_1_out_3;
  wire [15:0] R1_q, R2_q, R3_q, R4_q;

  Decoder #(.Selector_Bits(2)) decoder_1 (
    .sel(Reg_Write), .out_0(decoder_1_out_0), .out_1(decoder_1_out_1), .out_2(decoder_1_out_2),
    .out_3(decoder_1_out_3));
  Register #(.Bits(16)) R1 (.D(data), .C(CLK), .en(decoder_1_out_0), .Q(R1_q));
  Register #(.Bits(16)) R2 (.D(data), .C(CLK), .en(decoder_1_out_1), .Q(R2_q));
  Register #(.Bits(16)) R3 (.D(data), .C(CLK), .en(decoder_1_out_2), .Q(R3_q));
  Register #(.Bits(16)) R4 (.D(data), .C(CLK), .en(decoder_1_out_3), .Q(R4_q));
  Multiplexer #(.Selector_Bits(2), .Bits(16)) multiplexer_1 (
    .sel(Reg_1_Read), .in_0(R1_q), .in_1(R2_q), .in_2(R3_q), .in_3(R4_q), .out(Reg_1_Value));
  Multiplexer #(.Selector_Bits(2), .Bits(16)) multiplexer_2 (
    .sel(Reg_2_Read), .in_0(R1_q), .in_1(R2_q), .in_2(R3_q), .in_3(R4_q), .out(Reg_2_Value));
endmodule
